// Logisim project main.circ as structural Verilog
module \not  (
  input  in_1,
  output out_2
);

  nand nand_1 (out_2, in_1, in_1);
endmodule

module or_a (
  input  a,
  input  b,
  output out
);

  wire not_1_out, not_2_out;

  not not_1 (not_1_out, a);
  not not_2 (not_2_out, b);
  nand nand_1 (out, not_1_out, not_2_out);
endmodule

module or_b (
  input  a,
  input  b,
  output out_3
);

  wire nand_1_out, nand_2_out;

  nand nand_1 (nand_1_out, a, a);
  nand nand_2 (nand_2_out, b, b);
  nand nand_3 (out_3, nand_1_out, nand_2_out);
endmodule

module \and  (
  input  a,
  input  b,
  output out_3
);

  wire nand_1_out;

  nand nand_1 (nand_1_out, a, b);
  nand nand_2 (out_3, nand_1_out, nand_1_out);
endmodule

module xor_a (
  input  a,
  input  b,
  output out_3
);

  wire and_1_out, not_1_out, or_1_out, or_2_out;

  and and_1 (and_1_out, a, b);
  or or_1 (or_1_out, a, b);
  not not_1 (not_1_out, or_1_out);
  or or_2 (or_2_out, and_1_out, not_1_out);
  not not_2 (out_3, or_2_out);
endmodule

module xor_b (
  input  a,
  input  b,
  output out_3
);

  wire and_1_out, and_2_out, not_1_out, not_2_out;

  not not_1 (not_1_out, a);
  not not_2 (not_2_out, b);
  and and_1 (and_1_out, a, not_2_out);
  and and_2 (and_2_out, not_1_out, b);
  or or_1 (out_3, and_1_out, and_2_out);
endmodule

module mux (
  input  a,
  input  b,
  input  sel,
  output out
);

  wire and_1_out, and_2_out, not_1_out;

  not not_1 (not_1_out, sel);
  and and_1 (and_1_out, a, not_1_out);
  and and_2 (and_2_out, b, sel);
  or or_1 (out, and_1_out, and_2_out);
endmodule

module dmux (
  input  in,
  input  sel,
  output a,
  output b
);

  wire not_1_out;

  not not_1 (not_1_out, sel);
  and and_1 (a, in, not_1_out);
  and and_2 (b, in, sel);
endmodule

module not16 (
  input  [15:0] in_1,
  output [15:0] out_2
);

  not not_1 (out_2[0], in_1[0]);
  not not_2 (out_2[1], in_1[1]);
  not not_3 (out_2[2], in_1[2]);
  not not_4 (out_2[3], in_1[3]);
  not not_5 (out_2[4], in_1[4]);
  not not_6 (out_2[5], in_1[5]);
  not not_7 (out_2[6], in_1[6]);
  not not_8 (out_2[7], in_1[7]);
  not not_9 (out_2[8], in_1[8]);
  not not_10 (out_2[9], in_1[9]);
  not not_11 (out_2[10], in_1[10]);
  not not_12 (out_2[11], in_1[11]);
  not not_13 (out_2[12], in_1[12]);
  not not_14 (out_2[13], in_1[13]);
  not not_15 (out_2[14], in_1[14]);
  not not_16 (out_2[15], in_1[15]);
endmodule

module dmux4way (
  input  in,
  input  [1:0] in_2,
  output a,
  output b,
  output c,
  output d
);

  wire demultiplexer_1_out0, demultiplexer_1_out1;

  Demultiplexer demultiplexer_1 (
    .out0(demultiplexer_1_out0), .out1(demultiplexer_1_out1), .in(in), .sel(in_2[1]));  // open: en
  Demultiplexer demultiplexer_2 (.out0(a), .out1(b), .in(demultiplexer_1_out0), .sel(in_2[0]));  // open: en
  Demultiplexer demultiplexer_3 (.out0(c), .out1(d), .in(demultiplexer_1_out1), .sel(in_2[0]));  // open: en
endmodule

// HA
module halfAdder (
  input  a,
  input  b,
  output sum,
  output carry
);

  xor xor_1 (sum, a, b);
  and and_1 (carry, a, b);
endmodule

module fullAdder (
  input  c,
  input  a,
  input  b,
  output sum,
  output carry
);

  wire halfadder_1_carry, halfadder_1_sum, halfadder_2_carry;

  halfAdder halfadder_1 (.a(a), .b(b), .sum(halfadder_1_sum), .carry(halfadder_1_carry));
  halfAdder halfadder_2 (.a(c), .b(halfadder_1_sum), .sum(sum), .carry(halfadder_2_carry));
  or or_1 (carry, halfadder_2_carry, halfadder_1_carry);
endmodule

module ALU (
  input  zx__zero_x_input,
  input  nx__negate_x_input,
  input  [15:0] x,
  input  no__negate_the_output,
  input  [15:0] y,
  input  f__1__x___y___0__x____y,
  input  zy__zero_y_input,
  input  ny__negate_y_input,
  output [15:0] out,
  output ng__1_if_negative_number,
  output zr__1_if_zero
);

  wire or_1_out;
  wire [15:0] adder_1_out, and_1_out, multiplexer_1_out, multiplexer_2_out, multiplexer_3_out,
       multiplexer_4_out, multiplexer_5_out, not_1_out, not_2_out, not_3_out;

  Multiplexer #(.width(16), .enable("false")) multiplexer_1 (
    .in0(x), .in1({16{1'b0}}), .out(multiplexer_1_out), .sel(zx__zero_x_input));
  Multiplexer #(.width(16), .enable("false")) multiplexer_2 (
    .in0(y), .in1({16{1'b0}}), .out(multiplexer_2_out), .sel(zy__zero_y_input));
  assign not_1_out = ~multiplexer_1_out;  // NOT_Gate not_1, 16 bits wide
  assign not_2_out = ~multiplexer_2_out;  // NOT_Gate not_2, 16 bits wide
  Multiplexer #(.width(16), .enable("false")) multiplexer_3 (
    .in0(multiplexer_1_out), .in1(not_1_out), .out(multiplexer_3_out), .sel(nx__negate_x_input));
  Multiplexer #(.width(16), .enable("false")) multiplexer_4 (
    .in0(multiplexer_2_out), .in1(not_2_out), .out(multiplexer_4_out), .sel(ny__negate_y_input));
  assign and_1_out = multiplexer_3_out & multiplexer_4_out;  // AND_Gate and_1, 16 bits wide
  Adder #(.width(16)) adder_1 (.a(multiplexer_3_out), .b(multiplexer_4_out), .out(adder_1_out));  // open: cin, cout
  Multiplexer #(.width(16), .enable("false")) multiplexer_5 (
    .in0(and_1_out), .in1(adder_1_out), .out(multiplexer_5_out), .sel(f__1__x___y___0__x____y));
  assign not_3_out = ~multiplexer_5_out;  // NOT_Gate not_3, 16 bits wide
  or or_1 (or_1_out, out[0], out[1], out[2], out[3], out[4], out[5], out[6], out[7], out[8], out[9], out[10], out[11], out[12], out[13], out[14], ng__1_if_negative_number);
  Multiplexer #(.width(16), .enable("false")) multiplexer_6 (
    .in0(multiplexer_5_out), .in1(not_3_out), .out({ng__1_if_negative_number, out[14:0]}),
    .sel(no__negate_the_output));
  not not_4 (zr__1_if_zero, or_1_out);

  assign out[15] = ng__1_if_negative_number;
endmodule

module Bit (
  input  in,
  input  load,
  output out
);

  wire clock_1_out, multiplexer_1_out;

  Multiplexer #(.enable("false")) multiplexer_1 (.in0(out), .in1(in), .out(multiplexer_1_out), .sel(load));
  Clock clock_1 (.out(clock_1_out));
  D_Flip_Flop d_ff_1 (.clk(clock_1_out), .D(multiplexer_1_out), .Q(out));  // open: Qn, preset, en, reset
endmodule

module PC (
  input  load,
  input  reset,
  input  in,
  input  [15:0] in_2,
  output [15:0] out
);

  wire clock_1_out;
  wire [15:0] adder_1_out, multiplexer_1_out, multiplexer_2_out, multiplexer_3_out;

  Multiplexer #(.width(16), .enable("false")) multiplexer_1 (
    .in0(out), .in1(adder_1_out), .out(multiplexer_1_out), .sel(in));
  Adder #(.width(16)) adder_1 (.a(16'h1), .b(out), .out(adder_1_out), .cin(1'b0));  // open: cout
  Multiplexer #(.width(16), .enable("false")) multiplexer_2 (
    .in0(multiplexer_1_out), .in1(in_2), .out(multiplexer_2_out), .sel(load));
  Multiplexer #(.width(16), .enable("false")) multiplexer_3 (
    .in0(multiplexer_2_out), .in1({16{1'b0}}), .out(multiplexer_3_out), .sel(reset));
  Register #(.width(16)) register_1 (.D(multiplexer_3_out), .en(1'b1), .Q(out), .clk(clock_1_out));  // open: clr
  Clock clock_1 (.out(clock_1_out));
endmodule

module CPU (
  input  [15:0] inM,
  input  [15:0] instruction,
  input  reset,
  output [15:0] outM,
  output writeM,
  output [14:0] addressM,
  output [14:0] pc
);

  wire and_1_out, and_2_out, and_3_out, and_4_out, cAorM, cDestA, cDestD, clock_1_out, clock_2_out,
       clock_3_out, neg, not_1_out, not_2_out, not_3_out, or_1_out, or_2_out, zero;
  wire [2:0] cJump;
  wire [5:0] cOpCode;
  wire [15:0] aOrMOut, dOut, multiplexer_3_out;
  wire [15:13] multiplexer_2_out;
  wire [15:15] aOut, counter_1_q;

  Multiplexer #(.width(16), .enable("false")) multiplexer_1 (
    .in0({aOut[15], addressM}), .in1(inM), .out(aOrMOut), .sel(cAorM));
  not not_1 (not_1_out, instruction[15]);
  Multiplexer #(.width(16), .enable("false")) multiplexer_2 (
    .in0({16{1'b0}}), .in1(instruction),
    .out({multiplexer_2_out, cAorM, cOpCode, cDestA, cDestD, writeM, cJump}), .sel(instruction[15]));
  Multiplexer #(.width(16), .enable("false")) multiplexer_3 (
    .in0(instruction), .in1(outM), .out(multiplexer_3_out), .sel(instruction[15]));
  Clock clock_1 (.out(clock_1_out));
  or or_1 (or_1_out, not_1_out, cDestA);
  Register #(.width(16)) A_Register (
    .D(multiplexer_3_out), .en(or_1_out), .Q({aOut[15], addressM}), .clk(clock_1_out));  // open: clr
  ALU alu_1 (
    .x(dOut), .y(aOrMOut), .out(outM), .ng__1_if_negative_number(neg), .zr__1_if_zero(zero),
    .zx__zero_x_input(cOpCode[5]), .nx__negate_x_input(cOpCode[4]), .no__negate_the_output(cOpCode[0]),
    .zy__zero_y_input(cOpCode[3]), .ny__negate_y_input(cOpCode[2]), .f__1__x___y___0__x____y(cOpCode[1]));
  not not_2 (not_2_out, zero);
  and and_1 (and_1_out, not_2_out, not_3_out);
  not not_3 (not_3_out, neg);
  Register #(.width(16)) D_Register (.D(outM), .en(cDestD), .Q(dOut), .clk(clock_2_out));  // open: clr
  Clock clock_2 (.out(clock_2_out));
  and and_2 (and_2_out, cJump[0], neg);
  and and_3 (and_3_out, cJump[1], zero);
  or or_2 (or_2_out, and_2_out, and_3_out, and_4_out);
  and and_4 (and_4_out, cJump[2], and_1_out);
  Counter #(.width(16), .max('hffff)) counter_1 (
    .load(or_2_out), .D({aOut[15], addressM}), .count(1'b1), .Q({counter_1_q[15], pc}), .clk(clock_3_out),
    .clr(reset));  // open: carry
  Clock clock_3 (.out(clock_3_out));

  // Other names for the same wires on the sheet: cDestM = writeM; ALUOut[15:0] = outM; aOut[14:0] = addressM;
  //   aOutSplit[14:0] = addressM; instruct[15:0] = instruction; cType = instruction[15]
endmodule
